# Fritzing sketch briefkasten (saved by Fritzing 0.9.3b)
breadboards: 1

parts:
  WeMos_D1_Mini1 = WeMos D1 Mini
  VCC1 = 4 x AAA Battery Mount
  R2 = Resistor [tolerance=±5% resistance=100k package="2512 [SMD]"]
  R3 = Resistor [tolerance=±5% resistance=220 package=THT]
  Q1 = NPN-Transistor [package="TO92 [THT]"]
  S1 = SWITCH-MOMENTARY-2 [package=reed_switch_plastic]

nets:
  N1: WeMos_D1_Mini1.5V, VCC1.+, R2.Pin_1, R3.Pin_1, S1.1
  N2: WeMos_D1_Mini1.A0, R2.Pin_0
  N3: WeMos_D1_Mini1.G, VCC1.-, Q1.B
  N4: WeMos_D1_Mini1.RST, Q1.C
  N5: R3.Pin_0, Q1.E, S1.2

// code stored in the sketch: Breifkasten.ino
#include <ESP8266WiFi.h>
#include <IFTTTWebhook.h>

#define wlan_ssid "kjhome.wan"
#define wlan_pass "0009479163"
#define myKey "d1o-8g4PsXOGZ-FfbnVqqe"
#define brief "Briefmelder"
#define host "maker.ifttt.com"
int analogValue = 0;
float voltage = 0;
WiFiClient client;


void setup()
{
  pinMode(A0, INPUT);
  pinMode(BUILTIN_LED, OUTPUT);
  Serial.begin(9600);
  WiFi.begin(wlan_ssid, wlan_pass);
  while (WiFi.status() != WL_CONNECTED)
  {
    delay(500);
    Serial.print(".");
  }
  Serial.print("Wlan verbunden mit der IP:");
  Serial.print(WiFi.localIP());
  //IFTTTWebhook breifmelder(myKey, brief);
  //breifmelder.trigger();
  client.connect(host, 80);
  String url = "/trigger/Briefmelder/with/key/";
  url+=myKey;
  client.print(String("GET ") + url +" HTTP/1.1\r\n" + "Host: " + host "\r\n" + "Connection: close\r\n" + "\r\n");
  while (client.connected() || client.available())
{
  if (client.available())
  {
    String line = client.readStringUntil('\n');
    Serial.println(line);
  }
}  
  


}

void loop(){

  analogValue = analogRead(A0);
  Serial.print(analogValue);
  voltage = analogValue/1023;
  voltage = 4.2*voltage;
  Serial.print(voltage);
  delay(500);
  if (voltage <= 3.9)
  {
    //IFTTTWebhook battery(myKey, "battery_melder");
    //battery.trigger();
    client.connect(host, 80);
    String url = "/trigger/Battery_Melder/with/key/";
    url+=myKey;
    client.print(String("GET ") + url +" HTTP/1.1\r\n" + "Host: " + host "\r\n" + "Connection: close\r\n" + "\r\n");
    
    while (client.connected() || client.available())
    {
      if (client.available())
      {
        String line = client.readStringUntil('\n');
        Serial.println(line);
      }
    }  

    
    delay(5000);
  }
  digitalWrite(BUILTIN_LED, HIGH);
  ESP.deepSleep(0);
  
  

}
